# Fritzing sketch Air-Link_SchemaElettrico (saved by Fritzing 1.0.7)

parts:
  Mod1 = Amica NodeMCU DEVKIT 1.0
  Componente1 = BME280 Breakout
  DHT1 = DHT22 Humidity and Temperature Sensor
  PV1 = Small 6V Solar Panel [mn=? mpn=? part_number=?]  # not connected
  A1 = Waveshare solar power manager
  YL-83_-_Control_Board2 = YL-83 Rain Sensor - Control Board
  YL-83_-_Detection_Board2 = YL-83 Rain Sensor - Detection Board
  M1 = CK-07 [package=THT]
  R1 = Photocell (LDR) [power=0.25W dark_resistance_@0.01lx=300kΩ light_resistance_@100lx=400Ω luminance=10lx package=THT]
  Sensor1 = Gas Sensor Breakout Board
  U1 = LIPO-2000mAh [package=lipo-2000]

nets:
  VDD: Mod1.pin1, Mod1.pin_10, Mod1.pin_26, DHT1.VDD, YL-83_-_Control_Board2.VCC, M1.pin_4
  GND: Mod1.pin2, Mod1.pin_9, Mod1.pin_25, Mod1.pin_29, Componente1.GND, DHT1.GND, YL-83_-_Control_Board2.GND, M1.pin_3, Sensor1.GND
  N1: Mod1.pin7, Componente1.SDI/SDA
  N2: Mod1.pin8, Componente1.SCK/SCL
  N3: Mod1.pin_12, YL-83_-_Control_Board2.AO
  N4: Mod1.pin_13, DHT1.DATA
  N5: Mod1.pin_14, M1.pin_1
  N6: Mod1.pin_16, Sensor1.DOUT
  3.3V: Mod1.pin_30, Componente1.3.3V, Sensor1.5V
  N7: A1.Pin_1, U1.+
  N8: YL-83_-_Control_Board2.POS, YL-83_-_Detection_Board2.NEG
  N9: YL-83_-_Control_Board2.NEG, YL-83_-_Detection_Board2.POS
  N10: M1.pin_5, R1.pin_0
  N11: M1.pin_6, R1.pin_1

notes:
  6v 4800 mah

custom parts:
  Waveshare solar power manager: This solar power management module is designed for 6V~24V solar panel. It can charge the 3.7V rechargeable Li battery through solar panel or USB connection, and provides 5V/1A or 3.3V/1A regulated output.
  YL-83 Rain Sensor - Control Board: The YL-83 is a rain sensor that has more resistance when dry and less resistance when wet. The module runs at 5V.
  YL-83 Rain Sensor - Detection Board: The YL-83 is a rain sensor that has more resistance when dry and less resistance when wet. The module runs at 5V.
  CK-07: Fc-51 Infrared Obstacle Avoidance Proximity Sensor module. IR transmitter led, receiver LED, lm393 compaitor and a pot. 3.3 V to 5V power.
  Gas Sensor Breakout Board: Gas sensor breakout board. Input voltage is 5V. Sensor output is available in analog and digital.
